# Fritzing sketch og-001 (saved by Fritzing 0.9.3b)
circuit board: 3.67985cm x 1.42962cm

parts:
  Grove1 = Grove Button
  Grove2 = Grove Button
  Grove3 = Grove Button
  obniz = male pin header, 12 pins [form="♂ (male)"]

nets:
  N1: Grove1.GND, obniz.pin12
  N2: Grove1.VCC, obniz.pin11
  N3: Grove1.NC, obniz.pin10
  N4: Grove1.SIG, obniz.pin9
  N5: Grove2.GND, obniz.pin8
  N6: Grove2.VCC, obniz.pin7
  N7: Grove2.NC, obniz.pin6
  N8: Grove2.SIG, obniz.pin5
  N9: Grove3.GND, obniz.pin4
  N10: Grove3.VCC, obniz.pin3
  N11: Grove3.NC, obniz.pin2
  N12: Grove3.SIG, obniz.pin1

notes:
  0
  1ft-seabass.board og-01
  11
